// Logisim project modelagem_equacao.circ as structural Verilog: 1 circuit, main circuit main
module main (
  input  A,
  input  B,
  input  C,
  input  D,
  input  E
);

  wire and_1_out, and_2_out, not_1_out, or_1_out, or_2_out;

  and and_1 (and_1_out, A, B);
  not not_1 (not_1_out, C);
  or or_1 (or_1_out, D, E);
  and and_2 (and_2_out, and_1_out, not_1_out);
  or or_2 (or_2_out, and_2_out, or_1_out);
  LED led_1 (.in(or_2_out));

  // Notes on the sheet:
  //   S2 (!C)
  //   S1 (A.B)
  //   S3 (D+E)
  //   S = (((A.B).(!C))+(D+E))
  //   S4 (S1.S2)
  //   S (S4+S3)
endmodule
