// Logisim project modelagem_ropckrio.circ as structural Verilog: 1 circuit, main circuit main
module main (
  input  A,
  input  B,
  input  C,
  input  D
);

  wire and_1_out, and_2_out, or_1_out;

  and and_1 (and_1_out, A, B);
  or or_1 (or_1_out, C, D);
  and and_2 (and_2_out, and_1_out, or_1_out);
  LED led_1 (.in(and_2_out));

  // Notes on the sheet:
  //   S1
  //   S2
  //   S
endmodule
